// Logisim project intro.circ as structural Verilog: 1 circuit, main circuit main
module main (
  input  in_1,
  input  in_2,
  input  in_3,
  input  in_4,
  input  in_5,
  input  in_6,
  input  in_7,
  input  in_8,
  input  in_9,
  output out_10,
  output out_11,
  output out_12,
  output out_13
);

  wire and_2_out, and_3_out;

  and and_1 (out_12, in_5, in_8);
  // NAND_Gate nand_1 is placed but not wired
  and and_2 (and_2_out, in_2, in_3);
  and and_3 (and_3_out, and_2_out, in_4);
  or or_1 (out_13, in_6, in_9);
  // NOR_Gate nor_1 is placed but not wired
  xor xor_1 (out_10, in_1, and_3_out);
  not not_1 (out_11, in_7);
  // XOR_Gate xor_2 is placed but not wired

  // Notes on the sheet:
  //   AND
  //   NAND
  //   OR
  //   NOR
  //   NOT
  //   XOR
endmodule
